# Fritzing sketch tgs4161 (saved by Fritzing 0.9.2b)
breadboards: 1

parts:
  Part1 = Arduino Uno (Rev3)
  U1 = mystery part, 5 pins [chip_label=TGS4161]

nets:
  N1: Part1.A0, U1.pin3
  N2: Part1.5V, U1.pin5
  N3: Part1.GND, U1.pin2
